// Logisim project 1bitadder.circ as structural Verilog: 1 circuit, main circuit main
module main (
  input  A,
  input  B
);

  // XOR_Gate xor_1 has open pins: in0=A, in1=B, out=open
endmodule
