// Logisim project test.circ as structural Verilog: 1 circuit, main circuit main
module main (
  input  fsf2,
  input  fsf,
  output out2
);

  wire and_1_out;

  and and_1 (and_1_out, fsf2, fsf);
endmodule
